// Logisim project 8_Bit_CPU.circ as structural Verilog: 1 circuit, main circuit main
module main (
  input  WRITE_EN,
  input  in_2,
  input  in_3,
  input  in_4,
  input  in_5,
  input  in_6,
  input  in_7,
  input  in_8,
  input  ADD_SUB,
  input  in_10,
  input  in_11,
  input  in_12,
  input  in_13,
  input  lsb_hh,
  input  in_15,
  input  in_16,
  input  in_17,
  input  in_18,
  input  in_19,
  input  in_20,
  input  in_21,
  input  JUMP_LOAD,
  input  in_23,
  input  in_24,
  input  in_25,
  input  in_26,
  input  in_27,
  input  in_28,
  input  in_29,
  input  in_30,
  input  in_31,
  input  in_32,
  input  in_33,
  input  in_34,
  input  in_35,
  input  in_36,
  input  in_37,
  input  in_38,
  input  in_39,
  input  in_40,
  input  CTRL_SIGNAL_IN,
  input  CLOCK_IN,
  input  LSB_TO_BUS,
  input  LSB_FROM_BUS,
  input  in_45,
  input  in_46,
  input  in_47,
  input  in_48,
  input  in_49,
  input  in_50,
  input  in_51,
  input  in_52,
  input  in_53,
  input  in_54,
  input  in_55,
  input  in_56,
  input  TOGGLER_DIP_OR_REG,
  input  in_58,
  input  in_59,
  input  in_60,
  input  in_61,
  input  in_62,
  input  in_63,
  input  in_64,
  input  in_65,
  input  in_66,
  input  in_67,
  input  in_68,
  input  in_69,
  output [7:0] out_70
);

  wire ADD_IN_sw1, ADD_IN_sw2, ADD_IN_sw3, ADD_IN_sw4, and_2_out, and_3_out, CLK, dipswitch_1_sw7,
       j_k_ff_1_q, j_k_ff_1_qn, j_k_ff_2_q, j_k_ff_2_qn, j_k_ff_3_q, j_k_ff_3_qn, j_k_ff_4_qn, n74157_1_pin2,
       n74157_1_pin3, n74157_1_pin5, n74157_1_pin6, n74157_1_pin10, n74157_1_pin11, n74157_1_pin13,
       n74157_1_pin14, n74157_1_pin15, n74157_2_pin2, n74157_2_pin3, n74157_2_pin5, n74157_2_pin6,
       n74157_2_pin10, n74157_2_pin11, n74157_2_pin13, n74157_2_pin14, n74157_3_pin3, n74157_3_pin6,
       n74157_3_pin10, n74157_3_pin13, n74157_3_pin15, n74157_4_pin3, n74157_4_pin4, n74157_4_pin15,
       n74163_1_pin9, n74163_2_pin1, n74163_2_pin2, n74163_2_pin11, n74241_1_pin15, n74241_1_pin16,
       n74241_1_pin17, n74241_1_pin18, n74241_2_pin15, n74241_2_pin16, n74241_2_pin17, n74241_2_pin18,
       n74241_6_pin12, n74241_6_pin14, n74241_6_pin16, n74241_6_pin18, n74241_7_pin2, n74241_7_pin4,
       n74241_7_pin6, n74241_7_pin8, n74241_8_pin2, n74241_8_pin4, n74241_8_pin6, n74241_8_pin8,
       n74241_9_pin2, n74241_9_pin3, n74241_9_pin4, n74241_9_pin5, n74241_9_pin6, n74241_9_pin7,
       n74241_9_pin8, n74241_9_pin9, n74241_9_pin12, n74241_9_pin14, n74241_9_pin16, n74241_9_pin18,
       n74241_10_pin2, n74241_10_pin4, n74241_10_pin6, n74241_10_pin8, n74241_11_pin2, n74241_11_pin4,
       n74241_11_pin6, n74241_11_pin8, n74241_12_pin12, n74241_12_pin14, n74241_12_pin16, n74241_13_pin12,
       n74241_13_pin14, n74241_13_pin16, n74241_13_pin18, n74283_1_pin2, n74283_1_pin6, n74283_1_pin9,
       n74283_1_pin11, n74283_1_pin15, n74283_2_pin2, n74283_2_pin6, n74283_2_pin11, n74283_2_pin15,
       not_2_out, RA1, RA2, RA3, RA4, RA5, RA6, RA7, RA8, RB1, RB2, RB3, RB4, RB5, RB6, RB7, RB8,
       shift_register_1_p1, shift_register_1_p2, undriven, undriven_2, undriven_3, undriven_4, undriven_5;
  wire [1:0] n74157_2_pin4, n74157_2_pin9, n74157_3_pin4, n74157_3_pin9, n74241_2_pin5, n74241_2_pin9,
       n74241_4_pin5, n74241_4_pin9, n74241_6_pin5, n74241_6_pin9;
  wire [3:0] d_ff_1_q, n74157_1_pin4, n74241_1_pin9, n74241_3_pin9, n74241_5_pin9, register_4_q;
  wire [7:0] register_3_q, register_5_q, register_6_q, rom_1_data, rom_2_data, rom_3_data, rom_4_data,
       rom_5_data, shift_register_1_p9;
  wire [9:7] n74163_2_pin14;

  Clock clock_1 (.out(CLK));
  DipSwitch dipswitch_1 (.sw7(dipswitch_1_sw7));  // open: sw1, sw2, sw3, sw4, sw5, sw6, sw8
  Register register_1 (
    .D({n74241_2_pin5, n74241_2_pin9, n74241_1_pin9}), .en(WRITE_EN), .clk(CLK),
    .Q({RA8, RA7, RA6, RA5, RA4, RA3, RA2, RA1}), .clr(in_4));
  Register register_2 (
    .D({n74241_4_pin5, n74241_4_pin9, n74241_3_pin9}), .en(in_5), .clk(CLK),
    .Q({RB8, RB7, RB6, RB5, RB4, RB3, RB2, RB1}), .clr(in_7));
  Register register_3 (
    .D({n74241_6_pin5, n74241_6_pin9, n74241_5_pin9}), .en(in_10), .clk(CLK), .Q(register_3_q), .clr(in_13));
  J_K_Flip_Flop j_k_ff_1 (
    .J(dipswitch_1_sw7), .K(dipswitch_1_sw7), .clk(CLK), .Q(j_k_ff_1_q), .Qn(j_k_ff_1_qn));  // open: preset, reset
  J_K_Flip_Flop j_k_ff_2 (
    .J(dipswitch_1_sw7), .K(dipswitch_1_sw7), .clk(j_k_ff_1_q), .Q(j_k_ff_2_q), .Qn(j_k_ff_2_qn));  // open: preset, reset
  J_K_Flip_Flop j_k_ff_3 (
    .J(dipswitch_1_sw7), .K(dipswitch_1_sw7), .clk(j_k_ff_2_q), .Q(j_k_ff_3_q), .Qn(j_k_ff_3_qn));  // open: preset, reset
  _74241 u_74241_1 (
    .pin1(in_2), .pin2(RA1), .pin3(n74241_1_pin9[3]), .pin4(RA2), .pin5(n74241_1_pin9[2]), .pin6(RA3),
    .pin7(n74241_1_pin9[1]), .pin8(RA4), .pin9(n74241_1_pin9[0]), .pin19(WRITE_EN), .pin18(n74241_1_pin18),
    .pin17(n74241_1_pin17), .pin16(n74241_1_pin16), .pin15(n74241_1_pin15), .pin14(n74241_1_pin15),
    .pin13(n74241_1_pin16), .pin12(n74241_1_pin17), .pin11(n74241_1_pin18));
  _74241 u_74241_2 (
    .pin1(in_2), .pin2(RA5), .pin3(n74241_2_pin5[1]), .pin4(RA6), .pin5(n74241_2_pin5[0]), .pin6(RA7),
    .pin7(n74241_2_pin9[1]), .pin8(RA8), .pin9(n74241_2_pin9[0]), .pin19(WRITE_EN), .pin18(n74241_2_pin18),
    .pin17(n74241_2_pin17), .pin16(n74241_2_pin16), .pin15(n74241_2_pin15), .pin14(n74241_2_pin15),
    .pin13(n74241_2_pin16), .pin12(n74241_2_pin17), .pin11(n74241_2_pin18));
  _74241 u_74241_3 (
    .pin1(in_6), .pin2(RB1), .pin3(n74241_3_pin9[3]), .pin4(RB2), .pin5(n74241_3_pin9[2]), .pin6(RB3),
    .pin7(n74241_3_pin9[1]), .pin8(RB4), .pin9(n74241_3_pin9[0]), .pin19(in_5), .pin18(n74241_1_pin18),
    .pin17(n74241_1_pin17), .pin16(n74241_1_pin16), .pin15(n74241_1_pin15), .pin14(n74241_1_pin15),
    .pin13(n74241_1_pin16), .pin12(n74241_1_pin17), .pin11(n74241_1_pin18));
  _74241 u_74241_4 (
    .pin1(in_6), .pin2(RB5), .pin3(n74241_4_pin5[1]), .pin4(RB6), .pin5(n74241_4_pin5[0]), .pin6(RB7),
    .pin7(n74241_4_pin9[1]), .pin8(RB8), .pin9(n74241_4_pin9[0]), .pin19(in_5), .pin18(n74241_2_pin18),
    .pin17(n74241_2_pin17), .pin16(n74241_2_pin16), .pin15(n74241_2_pin15), .pin14(n74241_2_pin15),
    .pin13(n74241_2_pin16), .pin12(n74241_2_pin17), .pin11(n74241_2_pin18));
  _74241 u_74241_5 (
    .pin1(in_11), .pin2(register_3_q[0]), .pin3(n74241_5_pin9[3]), .pin4(register_3_q[1]),
    .pin5(n74241_5_pin9[2]), .pin6(register_3_q[2]), .pin7(n74241_5_pin9[1]), .pin8(register_3_q[3]),
    .pin9(n74241_5_pin9[0]), .pin19(in_10), .pin18(n74241_1_pin18), .pin17(n74241_1_pin17),
    .pin16(n74241_1_pin16), .pin15(n74241_1_pin15), .pin14(n74241_1_pin15), .pin13(n74241_1_pin16),
    .pin12(n74241_1_pin17), .pin11(n74241_1_pin18));
  _74241 u_74241_6 (
    .pin1(in_11), .pin2(register_3_q[4]), .pin3(n74241_6_pin5[1]), .pin4(register_3_q[5]),
    .pin5(n74241_6_pin5[0]), .pin6(register_3_q[6]), .pin7(n74241_6_pin9[1]), .pin8(register_3_q[7]),
    .pin9(n74241_6_pin9[0]), .pin19(in_10), .pin18(n74241_6_pin18), .pin17(n74241_2_pin17),
    .pin16(n74241_6_pin16), .pin15(n74241_2_pin15), .pin14(n74241_6_pin14), .pin13(n74241_2_pin16),
    .pin12(n74241_6_pin12), .pin11(n74241_2_pin18));
  J_K_Flip_Flop j_k_ff_4 (
    .J(dipswitch_1_sw7), .K(dipswitch_1_sw7), .clk(j_k_ff_3_q), .Qn(j_k_ff_4_qn));  // open: Q, preset, reset
  _74377 u_74377_1 ();  // open: pin1, pin2, pin3, pin4, pin5, pin6, pin7, pin8, pin9, pin19, pin18, pin17, pin16, pin15, pin14, pin13, pin12, pin11
  // _74377 74377_2: pin names not known; wires that end beside it: 1'b1, 1'b0
  LED led_1 (.in(n74241_6_pin12));
  LED led_2 (.in(n74241_6_pin14));
  LED led_3 (.in(n74241_6_pin16));
  LED led_4 (.in(n74241_6_pin18));
  LED led_5 (.in(n74241_1_pin17));
  LED led_6 (.in(n74241_1_pin15));
  LED led_7 (.in(n74241_1_pin16));
  LED led_8 (.in(n74241_1_pin18));
  LED LSB_BUS (.in(n74241_1_pin18));
  LED led_9 (.in(n74241_1_pin16));
  LED led_10 (.in(n74241_1_pin15));
  LED led_11 (.in(n74241_1_pin17));
  LED led_12 (.in(n74241_2_pin18));
  LED led_13 (.in(n74241_2_pin16));
  LED led_14 (.in(n74241_2_pin15));
  LED MSB_BUS (.in(n74241_2_pin17));
  _74241 u_74241_7 (
    .pin1(in_3), .pin2(n74241_7_pin2), .pin4(n74241_7_pin4), .pin6(n74241_7_pin6), .pin8(n74241_7_pin8),
    .pin18(n74241_1_pin18), .pin16(n74241_1_pin16), .pin14(n74241_1_pin15), .pin12(n74241_1_pin17));  // open: pin3, pin5, pin7, pin9, pin19, pin17, pin15, pin13, pin11
  _74241 u_74241_8 (
    .pin1(in_3), .pin2(n74241_8_pin2), .pin4(n74241_8_pin4), .pin6(n74241_8_pin6), .pin8(n74241_8_pin8),
    .pin18(n74241_2_pin18), .pin16(n74241_2_pin16), .pin14(n74241_2_pin15), .pin12(n74241_2_pin17));  // open: pin3, pin5, pin7, pin9, pin19, pin17, pin15, pin13, pin11
  DipSwitch dipswitch_2 (
    .sw1(n74241_7_pin2), .sw2(n74241_7_pin4), .sw3(n74241_7_pin6), .sw4(n74241_7_pin8), .sw5(n74241_8_pin2),
    .sw6(n74241_8_pin4), .sw7(n74241_8_pin6), .sw8(n74241_8_pin8));
  _74157 u_74157_1 (
    .pin1(TOGGLER_DIP_OR_REG), .pin2(n74157_1_pin2), .pin3(n74157_1_pin3), .pin4(n74157_1_pin4[0]),
    .pin5(n74157_1_pin5), .pin6(n74157_1_pin6), .pin7(n74157_1_pin4[1]), .pin15(n74157_1_pin15),
    .pin14(n74157_1_pin14), .pin13(n74157_1_pin13), .pin12(n74157_1_pin4[3]), .pin11(n74157_1_pin11),
    .pin10(n74157_1_pin10), .pin9(n74157_1_pin4[2]));
  _74157 u_74157_2 (
    .pin1(TOGGLER_DIP_OR_REG), .pin2(n74157_2_pin2), .pin3(n74157_2_pin3), .pin4(n74157_2_pin4[0]),
    .pin5(n74157_2_pin5), .pin6(n74157_2_pin6), .pin7(n74157_2_pin4[1]), .pin15(n74157_1_pin15),
    .pin14(n74157_2_pin14), .pin13(n74157_2_pin13), .pin12(n74157_2_pin9[1]), .pin11(n74157_2_pin11),
    .pin10(n74157_2_pin10), .pin9(n74157_2_pin9[0]));
  _74241 u_74241_9 (
    .pin1(in_20), .pin2(n74241_9_pin2), .pin3(n74241_9_pin3), .pin4(n74241_9_pin4), .pin5(n74241_9_pin5),
    .pin6(n74241_9_pin6), .pin7(n74241_9_pin7), .pin8(n74241_9_pin8), .pin9(n74241_9_pin9),
    .pin19(JUMP_LOAD), .pin18(n74241_9_pin18), .pin17(in_17), .pin16(n74241_9_pin16), .pin15(in_16),
    .pin14(n74241_9_pin14), .pin13(in_15), .pin12(n74241_9_pin12), .pin11(lsb_hh));
  DipSwitch DATA_IN (
    .sw1(n74157_1_pin2), .sw2(n74157_1_pin5), .sw3(n74157_1_pin11), .sw4(n74157_1_pin14),
    .sw5(n74157_2_pin2), .sw6(n74157_2_pin5), .sw7(n74157_2_pin11), .sw8(n74157_2_pin14));
  _74163 u_74163_1 (
    .pin1(in_30), .pin2(CLK), .pin3(n74241_9_pin9), .pin4(n74241_9_pin7), .pin5(n74241_9_pin5),
    .pin6(n74241_9_pin3), .pin7(in_28), .pin14(n74241_9_pin2), .pin13(n74241_9_pin4), .pin12(n74241_9_pin6),
    .pin11(n74241_9_pin8), .pin10(in_18), .pin9(n74163_1_pin9));  // open: pin15
  DipSwitch #(.number(4)) ADD_IN (.sw1(ADD_IN_sw1), .sw2(ADD_IN_sw2), .sw3(ADD_IN_sw3), .sw4(ADD_IN_sw4));
  LED LSB (.in(n74241_1_pin18));
  LED led_15 (.in(n74241_1_pin16));
  LED led_16 (.in(n74241_1_pin15));
  LED led_17 (.in(n74241_1_pin17));
  LED led_18 (.in(n74241_2_pin18));
  LED led_19 (.in(n74241_2_pin16));
  LED led_20 (.in(n74241_2_pin15));
  LED MSB (.in(n74241_2_pin17));
  _74157 u_74157_3 (
    .pin1(TOGGLER_DIP_OR_REG), .pin2(ADD_IN_sw1), .pin3(n74157_3_pin3), .pin4(n74157_3_pin4[0]),
    .pin5(ADD_IN_sw2), .pin6(n74157_3_pin6), .pin7(n74157_3_pin4[1]), .pin15(n74157_3_pin15),
    .pin14(ADD_IN_sw4), .pin13(n74157_3_pin13), .pin12(n74157_3_pin9[1]), .pin11(ADD_IN_sw3),
    .pin10(n74157_3_pin10), .pin9(n74157_3_pin9[0]));
  not not_1 (n74163_1_pin9, JUMP_LOAD);
  not not_2 (not_2_out, in_45);
  _74241 u_74241_10 (
    .pin1(in_8), .pin2(n74241_10_pin2), .pin4(n74241_10_pin4), .pin6(n74241_10_pin6), .pin8(n74241_10_pin8),
    .pin18(n74241_1_pin18), .pin16(n74241_1_pin16), .pin14(n74241_1_pin15), .pin12(n74241_1_pin17));  // open: pin3, pin5, pin7, pin9, pin19, pin17, pin15, pin13, pin11
  _74241 u_74241_11 (
    .pin1(in_8), .pin2(n74241_11_pin2), .pin4(n74241_11_pin4), .pin6(n74241_11_pin6), .pin8(n74241_11_pin8),
    .pin18(n74241_2_pin18), .pin16(n74241_2_pin16), .pin14(n74241_2_pin15), .pin12(n74241_2_pin17));  // open: pin3, pin5, pin7, pin9, pin19, pin17, pin15, pin13, pin11
  _74157 u_74157_4 (
    .pin1(not_2_out), .pin2(in_45), .pin3(n74157_4_pin3), .pin4(n74157_4_pin4), .pin15(n74157_4_pin15));  // open: pin5, pin6, pin7, pin14, pin13, pin12, pin11, pin10, pin9
  _74283 u_74283_1 (
    .pin1(n74241_10_pin4), .pin2(n74283_1_pin2), .pin3(RA2), .pin4(n74241_10_pin2), .pin5(RA1),
    .pin6(n74283_1_pin6), .pin7(ADD_SUB), .pin15(n74283_1_pin15), .pin14(RA3), .pin13(n74241_10_pin6),
    .pin12(RA4), .pin11(n74283_1_pin11), .pin10(n74241_10_pin8), .pin9(n74283_1_pin9));
  xor xor_1 (n74283_1_pin6, RB1, ADD_SUB);
  LED LSB_ADR_REG (.in(n74157_3_pin4[0]));
  LED led_21 (.in(n74157_3_pin4[1]));
  xor xor_2 (n74283_1_pin2, RB2, ADD_SUB);
  xor xor_3 (n74283_1_pin15, RB3, ADD_SUB);
  LED led_22 (.in(n74157_3_pin9[0]));
  LED MSB_ADR_REG (.in(n74157_3_pin9[1]));
  _74175 u_74175_1 (
    .pin1(in_56), .pin2(n74157_3_pin3), .pin7(n74157_3_pin6), .pin15(n74157_3_pin13), .pin13(in_51),
    .pin12(in_48), .pin10(n74157_3_pin10), .pin9(in_54));  // open: pin3, pin4, pin5, pin6, pin14, pin11
  xor xor_4 (n74283_1_pin11, RB4, ADD_SUB);
  and and_1 (n74157_4_pin3, CTRL_SIGNAL_IN, CLOCK_IN);
  _74283 u_74283_2 (
    .pin1(n74241_11_pin4), .pin2(n74283_2_pin2), .pin3(RA6), .pin4(n74241_11_pin2), .pin5(RA5),
    .pin6(n74283_2_pin6), .pin7(n74283_1_pin9), .pin15(n74283_2_pin15), .pin14(RA7), .pin13(n74241_11_pin6),
    .pin12(RA8), .pin11(n74283_2_pin11), .pin10(n74241_11_pin8));  // open: pin9
  xor xor_5 (n74283_2_pin6, RB5, ADD_SUB);
  xor xor_6 (n74283_2_pin2, RB6, ADD_SUB);
  xor xor_7 (n74283_2_pin15, RB7, ADD_SUB);
  xor xor_8 (n74283_2_pin11, RB8, ADD_SUB);
  RAM ram_1 (
    .addr({in_52, in_50, in_49, in_47, n74157_3_pin9, n74157_3_pin4}), .we(n74157_4_pin4), .oe(in_53),
    .clk(in_55), .din({n74157_2_pin9, n74157_2_pin4, n74157_1_pin4}), .dout(out_70));
  ROM #(.addrWidth(11)) rom_1 (
    .addr({in_68, n74163_2_pin14, in_67, in_65, in_63, in_62, in_61, in_60, in_59}), .data(rom_1_data));
  and and_2 (and_2_out, in_12, d_ff_1_q[3]);
  D_Flip_Flop d_ff_1 (.D(in_21), .clk(in_12), .Q(d_ff_1_q[0]));  // open: Qn, preset, reset
  D_Flip_Flop d_ff_2 (.D(d_ff_1_q[0]), .clk(in_12), .Q(d_ff_1_q[1]));  // open: Qn, preset, reset
  Register #(.width(4)) register_4 (.D(d_ff_1_q), .en(and_2_out), .clk(in_12), .Q(register_4_q));  // open: clr
  D_Flip_Flop d_ff_3 (.D(d_ff_1_q[1]), .clk(in_12), .Q(d_ff_1_q[2]));  // open: Qn, preset, reset
  _74241 u_74241_12 (
    .pin1(in_46), .pin2(out_70[0]), .pin4(out_70[1]), .pin6(out_70[2]), .pin8(out_70[3]),
    .pin18(n74157_1_pin3), .pin16(n74241_12_pin16), .pin14(n74241_12_pin14), .pin12(n74241_12_pin12));  // open: pin3, pin5, pin7, pin9, pin19, pin17, pin15, pin13, pin11
  D_Flip_Flop d_ff_4 (.D(d_ff_1_q[2]), .clk(in_12), .Q(d_ff_1_q[3]));  // open: Qn, preset, reset
  _74241 u_74241_13 (
    .pin1(in_46), .pin2(out_70[4]), .pin4(out_70[5]), .pin6(out_70[6]), .pin8(out_70[7]),
    .pin18(n74241_13_pin18), .pin16(n74241_13_pin16), .pin14(n74241_13_pin14), .pin12(n74241_13_pin12));  // open: pin3, pin5, pin7, pin9, pin19, pin17, pin15, pin13, pin11
  _7_Segment_Display u_7_segment_display_1 (
    .g(rom_1_data[6]), .f(rom_1_data[5]), .a(rom_1_data[0]), .b(rom_1_data[1]), .e(rom_1_data[4]),
    .d(rom_1_data[3]), .c(rom_1_data[2]), .dp(undriven));
  _7_Segment_Display u_7_segment_display_2 ();  // open: g, f, a, b, e, d, c, dp
  _7_Segment_Display u_7_segment_display_3 (.g(in_58));  // open: f, a, b, e, d, c, dp
  _7_Segment_Display u_7_segment_display_4 ();  // open: g, f, a, b, e, d, c, dp
  // Shift_Register shift_register_1: pin names not known; wires that end beside it: shift_register_1_p1, shift_register_1_p2, in_19, shift_register_1_p1, in_23, in_26, in_27, shift_register_1_p2, shift_register_1_p9[0], shift_register_1_p9[1], shift_register_1_p9[2], shift_register_1_p9[3], shift_register_1_p9[4], shift_register_1_p9[5], shift_register_1_p9[6], shift_register_1_p9[7]
  _74163 u_74163_2 (
    .pin1(n74163_2_pin1), .pin2(n74163_2_pin2), .pin7(in_69), .pin14(n74163_2_pin14[7]),
    .pin13(n74163_2_pin14[8]), .pin12(n74163_2_pin14[9]), .pin11(n74163_2_pin11), .pin10(in_64), .pin9(in_66));  // open: pin3, pin4, pin5, pin6, pin15
  Clock clock_2 (.out(n74163_2_pin2));
  not not_3 (n74163_2_pin1, n74163_2_pin11);
  Register register_5 (.D(shift_register_1_p9), .en(in_33), .clk(in_26), .Q(register_5_q));  // open: clr
  ROM #(.addrWidth(10)) rom_2 (.addr({in_25, in_24, register_6_q}), .data(rom_2_data));
  _7_Segment_Display u_7_segment_display_5 (
    .g(rom_2_data[6]), .f(rom_2_data[5]), .a(rom_2_data[0]), .b(rom_2_data[1]), .e(rom_2_data[4]),
    .d(rom_2_data[3]), .c(rom_2_data[2]), .dp(undriven_2));
  ROM #(.addrWidth(10)) rom_3 (.addr({in_25, in_24, register_6_q}), .data(rom_3_data));
  Register register_6 (
    .D({in_38, in_37, in_36, in_35, in_34, in_32, in_31, in_29}), .en(in_39), .clk(and_3_out),
    .Q(register_6_q));  // open: clr
  and and_3 (and_3_out, CLK, in_40);
  _7_Segment_Display u_7_segment_display_6 (
    .g(rom_3_data[6]), .f(rom_3_data[5]), .a(rom_3_data[0]), .b(rom_3_data[1]), .e(rom_3_data[4]),
    .d(rom_3_data[3]), .c(rom_3_data[2]), .dp(undriven_3));
  ROM #(.addrWidth(10)) rom_4 (.addr({in_25, in_24, register_6_q}), .data(rom_4_data));
  _7_Segment_Display u_7_segment_display_7 (
    .g(rom_4_data[6]), .f(rom_4_data[5]), .a(rom_4_data[0]), .b(rom_4_data[1]), .e(rom_4_data[4]),
    .d(rom_4_data[3]), .c(rom_4_data[2]), .dp(undriven_4));
  ROM #(.addrWidth(10)) rom_5 (.addr({in_25, in_24, register_6_q}), .data(rom_5_data));
  _7_Segment_Display u_7_segment_display_8 (
    .g(rom_5_data[6]), .f(rom_5_data[5]), .a(rom_5_data[0]), .b(rom_5_data[1]), .e(rom_5_data[4]),
    .d(rom_5_data[3]), .c(rom_5_data[2]), .dp(undriven_5));
  // also tied to GND on the sheet: {n74157_1_pin15, n74157_3_pin15, n74157_4_pin15}

  // Other names for the same wires on the sheet: A = in_2; A1 = in_6; A3 = in_11; B = WRITE_EN; B1 = in_5; B3 = in_10

  // Notes on the sheet:
  //   REG B
  //   REG A
  //   PROGRAM COUNTER
  //   COUNT_OUT_EN_(ACT_0)
  //   RAM DIVISION
  //   ALU
  //   ADDRESS_REG
  //   contents of rom_1 (hex, n*v repeats v):
  //   40 6 5b 4f 66 6d 7d 7 7f 6f 77 7c 39 5e 79 71
  //   contents of rom_2 (hex, n*v repeats v):
  //   384*3f 128*40
  //   contents of rom_3 (hex, n*v repeats v):
  //   100*3f 100*6 56*5b 100*3f 57*6 99*3f
  //   contents of rom_4 (hex, n*v repeats v):
  //   10*3f 10*6 10*5b 10*4f 10*66 10*6d 10*7d 10*7 10*7f 10*6f 10*3f 10*6 10*5b 10*4f 10*66 10*6d 10*7d
  //   10*7 10*7f 10*6f 10*3f 10*6 10*5b 10*4f 10*66 6*6d 10*3f 10*6 10*5b 10*4f 10*66 10*6d 10*7d 10*7
  //   10*7f 10*6f 10*3f 10*6 17*5b 10*6 10*3f 10*6f 10*7f 10*7 10*7d 10*6d 10*66 10*4f 10*5b 10*6 9*3f
  //   contents of rom_5 (hex, n*v repeats v):
  //   3f 6 5b 4f 66 6d 7d 7 7f 6f 3f 6 5b 4f 66 6d 7d 7 7f 6f 3f 6 5b 4f 66 6d 7d 7 7f 6f 3f 6 5b 4f 66 6d
  //   7d 7 7f 6f 3f 6 5b 4f 66 6d 7d 7 7f 6f 3f 6 5b 4f 66 6d 7d 7 7f 6f 3f 6 5b 4f 66 6d 7d 7 7f 6f 3f 6
  //   5b 4f 66 6d 7d 7 7f 6f 3f 6 5b 4f 66 6d 7d 7 7f 6f 3f 6 5b 4f 66 6d 7d 7 7f 6f 3f 6 5b 4f 66 6d 7d 7
  //   7f 6f 3f 6 5b 4f 66 6d 7d 7 7f 6f 3f 6 5b 4f 66 6d 7d 7 7f 6f 3f 6 5b 4f 66 6d 7d 7 7f 6f 3f 6 5b 4f
  //   66 6d 7d 7 7f 6f 3f 6 5b 4f 66 6d 7d 7 7f 6f 3f 6 5b 4f 66 6d 7d 7 7f 6f 3f 6 5b 4f 66 6d 7d 7 7f 6f
  //   3f 6 5b 4f 66 6d 7d 7 7f 6f 3f 6 5b 4f 66 6d 7d 7 7f 6f 3f 6 5b 4f 66 6d 7d 7 7f 6f 3f 6 5b 4f 66 6d
  //   7d 7 7f 6f 3f 6 5b 4f 66 6d 7d 7 7f 6f 3f 6 5b 4f 66 6d 7d 7 7f 6f 3f 6 5b 4f 66 6d 7d 7 7f 6f 3f 6
  //   5b 4f 66 6d 3f 6 5b 4f 66 6d 7d 7 7f 6f 3f 6 5b 4f 66 6d 7d 7 7f 6f 3f 6 5b 4f 66 6d 7d 7 7f 6f 3f 6
  //   5b 4f 66 6d 7d 7 7f 6f 3f 6 5b 4f 66 6d 7d 7 7f 6f 3f 6 5b 4f 66 6d 7d 7 7f 6f 3f 6 5b 4f 66 6d 7d 7
  //   7f 6f 3f 6 5b 4f 66 6d 7d 7 7f 6f 3f 6 5b 4f 66 6d 7d 7 7f 6f 3f 6 5b 4f 66 6d 7d 7 7f 6f 3f 6 5b 4f
  //   66 6d 7d 7 7f 6f 3f 6 5b 4f 66 6d 7d 7 7f 6f 3f 6 5b 4f 66 6d 7d 7 7f 7 7d 6d 66 4f 5b 6 3f 6f 7f 7
  //   7d 6d 66 4f 5b 6 3f 6f 7f 7 7d 6d 66 4f 5b 6 3f 6f 7f 7 7d 6d 66 4f 5b 6 3f 6f 7f 7 7d 6d 66 4f 5b 6
  //   3f 6f 7f 7 7d 6d 66 4f 5b 6 3f 6f 7f 7 7d 6d 66 4f 5b 6 3f 6f 7f 7 7d 6d 66 4f 5b 6 3f 6f 7f 7 7d 6d
  //   66 4f 5b 6 3f 6f 7f 7 7d 6d 66 4f 5b 6 3f 6f 7f 7 7d 6d 66 4f 5b 6 3f 6f 7f 7 7d 6d 66 4f 5b 6 3f 6f
  //   7f 7 7d 6d 66 4f 5b 6
endmodule
